# Fritzing sketch nimbus (saved by Fritzing 0.8.7b)
breadboards: 1

parts:
  U1 = Spark Core (v1.0)
  LED1 = smd LED [color="Red (633nm)" package="0603 [SMD]"]
  DHT1 = DHT22 Humidity and Temperature Sensor
  U2 = mystery part, 1 pin [chip_label=GA1A12S202]
  U2_2 = mystery part, 3 pins [chip_label=GA1A12S202]
  R2 = Resistor [tolerance=±5% resistance=220 package=THT]
  R2_2 = Resistor [tolerance=±5% resistance=10k package=THT]
  R1 = Resistor [tolerance=±5% resistance=150 package=THT]
  R1_2 = Resistor [tolerance=±5% resistance=220 package=THT]
  R1_3 = Resistor [tolerance=±5% resistance=220 package=THT]

nets:
  N1: U1.A0, U2_2.pin2
  3V3: U1.A2, U1.3V3, DHT1.VDD, U2_2.pin3, R2.Pin_0, R2_2.Pin_0
  N2: U1.A3, U1.A6
  N3: U1.A5, U1.VIN
  GND: U1.GND, LED1.cathode, DHT1.GND, U2.pin1, U2_2.pin1
  N4: U1.D3, DHT1.DATA, R2.Pin_1, R2_2.Pin_1
  N5: U1.D6, R1.Pin_0, R1_2.Pin_0, R1_3.Pin_0
  N6: LED1.anode, R1.Pin_1, R1_2.Pin_1, R1_3.Pin_1

custom parts:
  Spark Core (v1.0): The Spark Core is a tiny Wi-Fi development board that makes it easy to create internet-connected hardware. The Core is all you need to get started; power it over USB and in minutes you'll be controlling LEDs, switches and motors and collecting data from sensors over the internet! It has 8 digital I/O pins, 8 analog I/O pins, 8 PWM pins; UART (Serial), SPI, I2C, and JTAG peripherals available.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
